// Logisim project cpu_design.circ as structural Verilog
module main (
  input  not_enable,
  input  [15:0] DATA_in,
  input  [15:0] FREQUENCY_in
);

  wire ALU_q, and_2_out, and_3_out, and_4_out, and_5_out, and_6_out, and_7_out, and_8_out, and_9_out,
       and_10_out, and_11_out, and_12_out, and_13_out, and_14_out, and_15_out, and_16_out, and_18_out,
       and_19_out, and_20_out, and_21_out, and_22_out, and_23_out, and_24_out, clk, clock_in_out,
       comparator_1_eq, comparator_2_eq, demultiplexer_1_out0, demultiplexer_1_out1, demultiplexer_1_out2,
       demultiplexer_1_out3, demultiplexer_1_out4, demultiplexer_1_out5, demultiplexer_1_out6,
       demultiplexer_1_out7, demultiplexer_1_out8, demultiplexer_1_out9, demultiplexer_1_out10,
       demultiplexer_1_out11, demultiplexer_1_out12, demultiplexer_1_out13, demultiplexer_1_out14,
       demultiplexer_1_out15, demultiplexer_2_out2, demultiplexer_3_out0, E_PC, IMM, INT, INTERNAL_ENABLE,
       LOAD_PC, MEM_q, nor_1_out, nor_2_out, nor_3_out, nor_4_out, nor_5_out, not_1_out, not_2_out,
       not_4_out, or_1_out, or_4_out, or_5_out, PC_carry, pull_resistor_7_node, pull_resistor_10_node,
       READ_SPECIAL_A, WRITE_SPECIAL;
  wire [0:0] rA_q;
  wire [3:0] A_q, multiplexer_8_out, SELECT_SPECIAL_REG;
  wire [4:0] controlled_buffer_2_out, instruction_q;
  wire [4:4] or_2_out;
  wire [10:0] undriven;
  wire [14:0] rA_q_2;
  wire [15:0] adder_1_out, and_17_out, controlled_buffer_1_out, controlled_buffer_4_out,
       controlled_buffer_5_out, d_ff_1_q, decoder_IR_q, fetch_IR_q, multiplexer_2_out, multiplexer_3_out,
       multiplexer_4_out, multiplexer_5_out, multiplexer_9_out, multiplexer_10_out, multiplexer_11_out,
       multiplexer_12_out, multiplexer_13_out, multiplexer_14_out, multiplexer_15_out, negator_1_out,
       not_3_out, or_6_out, PC_q, pull_resistor_5_node, pull_resistor_13_node, R1_q, R15_q, rA, rB, rB_q,
       register_1_q, register_2_q, register_3_q, register_4_q, register_5_q, register_6_q, register_7_q,
       register_8_q, register_9_q, register_10_q, register_11_q, register_12_q, register_13_q, shifter_1_out,
       SPECIAL_REG_OUT, subtractor_1_out, xor_1_out;

  Clock clock_in (.out(clock_in_out));
  nor nor_1 (nor_1_out, not_enable, INTERNAL_ENABLE);
  Pull_Resistor pull_resistor_1 (.node(INTERNAL_ENABLE));
  and and_1 (clk, clock_in_out, nor_1_out);
  Pull_Resistor pull_resistor_2 (.node(LOAD_PC));
  or or_1 (or_1_out, LOAD_PC, demultiplexer_1_out0);
  Demultiplexer #(.select(4)) demultiplexer_1 (
    .out0(demultiplexer_1_out0), .out1(demultiplexer_1_out1), .out2(demultiplexer_1_out2),
    .out3(demultiplexer_1_out3), .out4(demultiplexer_1_out4), .out5(demultiplexer_1_out5),
    .out6(demultiplexer_1_out6), .out7(demultiplexer_1_out7), .out8(demultiplexer_1_out8),
    .out9(demultiplexer_1_out9), .out10(demultiplexer_1_out10), .out11(demultiplexer_1_out11),
    .out12(demultiplexer_1_out12), .out13(demultiplexer_1_out13), .out14(demultiplexer_1_out14),
    .out15(demultiplexer_1_out15), .in(or_4_out), .sel(A_q));
  Pull_Resistor pull_resistor_3 (.node(DATA_in));
  Pull_Resistor pull_resistor_4 (.node(E_PC));
  Register #(.width(16)) R1 (.D(controlled_buffer_5_out), .en(demultiplexer_1_out1), .clk(clk), .Q(R1_q));  // open: clr
  Register #(.width(16)) register_1 (
    .D(controlled_buffer_5_out), .en(demultiplexer_1_out2), .clk(clk), .Q(register_1_q));  // open: clr
  Register #(.width(16)) register_2 (
    .D(controlled_buffer_5_out), .en(demultiplexer_1_out3), .clk(clk), .Q(register_2_q));  // open: clr
  Register #(.width(16)) register_3 (
    .D(controlled_buffer_5_out), .en(demultiplexer_1_out4), .clk(clk), .Q(register_3_q));  // open: clr
  Register #(.width(16)) register_4 (
    .D(controlled_buffer_5_out), .en(demultiplexer_1_out5), .clk(clk), .Q(register_4_q));  // open: clr
  Register #(.width(16)) register_5 (
    .D(controlled_buffer_5_out), .en(demultiplexer_1_out6), .clk(clk), .Q(register_5_q));  // open: clr
  Register #(.width(16)) register_6 (
    .D(controlled_buffer_5_out), .en(demultiplexer_1_out7), .clk(clk), .Q(register_6_q));  // open: clr
  Register #(.width(16)) register_7 (
    .D(controlled_buffer_5_out), .en(demultiplexer_1_out8), .clk(clk), .Q(register_7_q));  // open: clr
  Register #(.width(16)) register_8 (
    .D(controlled_buffer_5_out), .en(demultiplexer_1_out9), .clk(clk), .Q(register_8_q));  // open: clr
  Register #(.width(16)) register_9 (
    .D(controlled_buffer_5_out), .en(demultiplexer_1_out10), .clk(clk), .Q(register_9_q));  // open: clr
  Register #(.width(16)) register_10 (
    .D(controlled_buffer_5_out), .en(demultiplexer_1_out11), .clk(clk), .Q(register_10_q));  // open: clr
  Register #(.width(16)) register_11 (
    .D(controlled_buffer_5_out), .en(demultiplexer_1_out12), .clk(clk), .Q(register_11_q));  // open: clr
  Register #(.width(16)) register_12 (
    .D(controlled_buffer_5_out), .en(demultiplexer_1_out13), .clk(clk), .Q(register_12_q));  // open: clr
  Register #(.width(16)) register_13 (
    .D(controlled_buffer_5_out), .en(demultiplexer_1_out14), .clk(clk), .Q(register_13_q));  // open: clr
  Register #(.width(16)) R15 (
    .D(controlled_buffer_5_out), .en(demultiplexer_1_out15), .clk(clk), .Q(R15_q));  // open: clr
  Pull_Resistor pull_resistor_5 (.node(pull_resistor_5_node));
  Multiplexer #(.width(16)) multiplexer_1 (.in0(DATA_in), .in1(16'h9f00), .out(pull_resistor_5_node), .sel(INT));
  Pull_Resistor pull_resistor_6 (.node(INT));
  Pull_Resistor #(.pull(1)) pull_resistor_7 (.node(pull_resistor_7_node));
  Counter #(.max('hffff), .width(16)) PC (
    .load(or_1_out), .D(controlled_buffer_5_out), .count(E_PC), .Q(PC_q), .carry(PC_carry), .clk(clk));  // open: up, clr
  Register #(.width(16)) fetch_IR (
    .D(pull_resistor_5_node), .en(pull_resistor_7_node), .clk(clk), .Q(fetch_IR_q));  // open: clr
  Pull_Resistor pull_resistor_8 (.node(fetch_IR_q));
  assign controlled_buffer_1_out = not_1_out ? fetch_IR_q : 16'bz;  // Controlled_Buffer controlled_buffer_1
  not not_1 (not_1_out, IMM);
  Multiplexer #(.select(4), .width(16)) multiplexer_2 (
    .in0(PC_q), .in1(R1_q), .in2(register_1_q), .in3(register_2_q), .in4(register_3_q), .in5(register_4_q),
    .in6(register_5_q), .in7(register_6_q), .in8(register_7_q), .in9(register_8_q), .in10(register_9_q),
    .in11(register_10_q), .in12(register_11_q), .in13(register_12_q), .in14(register_13_q), .in15(R15_q),
    .out(multiplexer_2_out), .sel(decoder_IR_q[3:0]));
  Multiplexer #(.select(4), .width(16)) multiplexer_3 (
    .in0(PC_q), .in1(R1_q), .in2(register_1_q), .in3(register_2_q), .in4(register_3_q), .in5(register_4_q),
    .in6(register_5_q), .in7(register_6_q), .in8(register_7_q), .in9(register_8_q), .in10(register_9_q),
    .in11(register_10_q), .in12(register_11_q), .in13(register_12_q), .in14(register_13_q), .in15(R15_q),
    .out(multiplexer_3_out), .sel(decoder_IR_q[7:4]));
  Register #(.width(16)) decoder_IR (
    .D(controlled_buffer_1_out), .en(pull_resistor_10_node), .clk(clk), .Q(decoder_IR_q));  // open: clr
  Pull_Resistor pull_resistor_9 (.node(controlled_buffer_1_out));
  Pull_Resistor #(.pull(1)) pull_resistor_10 (.node(pull_resistor_10_node));
  Pull_Resistor pull_resistor_11 (.node(decoder_IR_q));
  Comparator #(.width(4)) comparator_1 (.a(decoder_IR_q[3:0]), .b(A_q), .eq(comparator_1_eq));  // open: gt, lt
  Comparator #(.width(4)) comparator_2 (.a(decoder_IR_q[7:4]), .b(A_q), .eq(comparator_2_eq));  // open: gt, lt
  Multiplexer #(.width(16)) multiplexer_4 (
    .in0(multiplexer_2_out), .in1(controlled_buffer_5_out), .out(multiplexer_4_out), .sel(and_2_out));
  and and_2 (and_2_out, comparator_1_eq, or_4_out);
  Multiplexer #(.width(16)) multiplexer_5 (
    .in0(multiplexer_3_out), .in1(controlled_buffer_5_out), .out(multiplexer_5_out), .sel(and_3_out));
  and and_3 (and_3_out, comparator_2_eq, or_4_out);
  and and_4 (and_4_out, decoder_IR_q[15], ~decoder_IR_q[14]);  // AND_Gate
  and and_5 (and_5_out, decoder_IR_q[12], ~decoder_IR_q[13]);  // AND_Gate
  and and_6 (and_6_out, decoder_IR_q[8], decoder_IR_q[9], decoder_IR_q[10], decoder_IR_q[11]);
  and and_7 (and_7_out, ~decoder_IR_q[8], decoder_IR_q[9], decoder_IR_q[10], decoder_IR_q[11]);  // AND_Gate
  nor nor_2 (nor_2_out, decoder_IR_q[7], decoder_IR_q[6], decoder_IR_q[5], decoder_IR_q[4]);
  Multiplexer #(.width(16)) multiplexer_6 (
    .in0(multiplexer_4_out), .in1(SPECIAL_REG_OUT), .out(rA), .sel(READ_SPECIAL_A));
  Pull_Resistor pull_resistor_12 (.node(READ_SPECIAL_A));
  Multiplexer #(.width(16)) multiplexer_7 (
    .in0(multiplexer_5_out), .in1(SPECIAL_REG_OUT), .out(rB), .sel(READ_SPECIAL_A));
  nor nor_3 (nor_3_out, decoder_IR_q[13], decoder_IR_q[12]);
  and and_8 (and_8_out, nor_3_out, and_6_out, nor_4_out);
  nor nor_4 (nor_4_out, decoder_IR_q[7], decoder_IR_q[6], decoder_IR_q[4]);
  and and_9 (and_9_out, nor_3_out, and_6_out);
  and and_10 (and_10_out, and_7_out, and_5_out);
  Multiplexer #(.width(4)) multiplexer_8 (
    .in0(decoder_IR_q[11:8]), .in1(decoder_IR_q[7:4]), .out(multiplexer_8_out), .sel(and_6_out));
  or or_2 (or_2_out[4], and_9_out, and_10_out);
  and and_11 (and_11_out, and_10_out, and_5_out, nor_2_out);
  assign controlled_buffer_2_out = nor_3_out ? {or_2_out[4], multiplexer_8_out} : 5'bz;  // Controlled_Buffer controlled_buffer_2
  or or_3 (IMM, and_8_out, and_11_out);
  Pull_Resistor pull_resistor_13 (.node(pull_resistor_13_node));
  assign pull_resistor_13_node = IMM ? fetch_IR_q : 16'bz;  // Controlled_Buffer controlled_buffer_3
  Multiplexer #(.width(16)) multiplexer_9 (
    .in0(rB), .in1(pull_resistor_13_node), .out(multiplexer_9_out), .sel(or_2_out[4]));
  Pull_Resistor pull_resistor_14 (.node(controlled_buffer_2_out));
  Register #(.width(16)) u_rB (.D(multiplexer_9_out), .en(and_4_out), .clk(clk), .Q(rB_q));  // open: clr
  Register #(.width(16)) u_rA (.D(rA), .en(and_4_out), .clk(clk), .Q({rA_q_2, rA_q[0]}));  // open: clr
  D_Flip_Flop ALU (.D(and_12_out), .clk(clk), .Q(ALU_q));  // open: Qn, preset, reset
  and and_12 (and_12_out, and_4_out, nor_3_out);
  Register #(.width(5)) instruction (
    .D(controlled_buffer_2_out), .en(and_4_out), .clk(clk), .Q(instruction_q));  // open: clr
  D_Flip_Flop MEM (.D(and_13_out), .clk(clk), .Q(MEM_q));  // open: Qn, preset, reset
  and and_13 (and_13_out, and_4_out, and_5_out);
  Register #(.width(4)) A (.D(decoder_IR_q[3:0]), .en(and_4_out), .clk(clk), .Q(A_q));  // open: clr
  and and_14 (and_14_out, MEM_q, or_5_out);
  or or_4 (or_4_out, and_14_out, ALU_q);
  Demultiplexer #(.select(4)) demultiplexer_2 (
    .out2(demultiplexer_2_out2), .in(WRITE_SPECIAL), .sel(SELECT_SPECIAL_REG));  // open: out0, out1, out3, out4, out5, out6, out7, out8, out9, out10, out11, out12, out13, out14, out15
  and and_15 (and_15_out, instruction_q[3], ALU_q);
  and and_16 (and_16_out, instruction_q[4], MEM_q);
  Demultiplexer #(.select(4)) demultiplexer_3 (
    .out0(demultiplexer_3_out0), .in(and_16_out), .sel(instruction_q[3:0]));  // open: out1, out2, out3, out4, out5, out6, out7, out8, out9, out10, out11, out12, out13, out14, out15
  assign controlled_buffer_4_out = not_2_out ? rB_q : 16'bz;  // Controlled_Buffer controlled_buffer_4
  not not_2 (not_2_out, instruction_q[4]);
  Pull_Resistor pull_resistor_15 (.node(rB_q));
  Pull_Resistor pull_resistor_16 (.node(rB_q));
  assign and_17_out = {rA_q_2, rA_q[0]} & rB_q;  // AND_Gate and_17, 16 bits wide
  assign xor_1_out = {rA_q_2, rA_q[0]} ^ rB_q;  // XOR_Gate xor_1, 16 bits wide
  Pull_Resistor pull_resistor_17 (.node(controlled_buffer_4_out));
  assign controlled_buffer_5_out = and_18_out ? rB_q : 16'bz;  // Controlled_Buffer controlled_buffer_5
  and and_18 (and_18_out, nor_5_out, MEM_q);
  nor nor_5 (nor_5_out, instruction_q[0], instruction_q[1], instruction_q[2], instruction_q[3], instruction_q[4]);
  Adder #(.width(16)) adder_1 (
    .a({rA_q_2, rA_q[0]}), .b(rB_q), .out(adder_1_out), .cin(instruction_q[0]));  // open: cout
  Subtractor #(.width(16)) subtractor_1 (
    .a({rA_q_2, rA_q[0]}), .b(rB_q), .out(subtractor_1_out), .bin(instruction_q[0]));  // open: bout
  Multiplexer #(.width(16)) multiplexer_10 (
    .in0(and_17_out), .in1(not_3_out), .out(multiplexer_10_out), .sel(instruction_q[4]));
  assign not_3_out = ~{rA_q_2, rA_q[0]};  // NOT_Gate not_3, 16 bits wide
  Shifter #(.shift("ar"), .width(16)) shifter_1 (.in({rA_q_2, rA_q[0]}), .\dist (4'b0001), .out(shifter_1_out));
  or or_5 (or_5_out, demultiplexer_3_out0, nor_5_out);
  assign controlled_buffer_5_out = demultiplexer_3_out0 ? rB_q : 16'bz;  // Controlled_Buffer controlled_buffer_6
  D_Flip_Flop d_ff_1 (.D(undriven[0]), .clk(and_19_out), .Q(d_ff_1_q[0]));  // open: Qn, preset, reset
  and and_19 (and_19_out, demultiplexer_2_out2, clk);
  D_Flip_Flop d_ff_2 (.D(undriven[1]), .clk(and_20_out), .Q(d_ff_1_q[1]));  // open: Qn, preset, reset
  and and_20 (and_20_out, demultiplexer_2_out2, clk);
  D_Flip_Flop d_ff_3 (.D(undriven[2]), .clk(and_21_out), .Q(d_ff_1_q[2]));  // open: Qn, preset, reset
  and and_21 (and_21_out, demultiplexer_2_out2, clk);
  D_Flip_Flop d_ff_4 (.D(undriven[9]), .clk(and_22_out), .Q(d_ff_1_q[9]));  // open: Qn, preset, reset
  and and_22 (and_22_out, demultiplexer_2_out2, clk);
  D_Flip_Flop d_ff_5 (.D(undriven[10]), .clk(and_23_out), .Q(d_ff_1_q[10]));  // open: Qn, preset, reset
  and and_23 (and_23_out, demultiplexer_2_out2, clk);
  assign or_6_out = {rA_q_2, rA_q[0]} | rB_q;  // OR_Gate or_6, 16 bits wide
  Negator #(.width(16)) negator_1 (.in({rA_q_2, rA_q[0]}), .out(negator_1_out));
  Multiplexer #(.width(16)) multiplexer_11 (
    .in0(xor_1_out), .out(multiplexer_11_out), .sel(instruction_q[0]));  // open: in1
  Multiplexer #(.width(16)) multiplexer_12 (
    .in0({rA_q_2[13:0], rA_q[0], controlled_buffer_4_out[15]}), .in1({controlled_buffer_4_out[0], rA_q_2}),
    .out(multiplexer_12_out), .sel(instruction_q[0]));
  Multiplexer #(.width(16)) multiplexer_13 (
    .in0(shifter_1_out), .out(multiplexer_13_out), .sel(instruction_q[0]));  // open: in1
  and and_24 (and_24_out, ALU_q, not_4_out);
  Multiplexer #(.width(16)) multiplexer_14 (
    .in0(multiplexer_10_out), .in1(multiplexer_15_out), .out(multiplexer_14_out), .sel(instruction_q[0]));
  Multiplexer #(.width(16)) multiplexer_15 (
    .in0(or_6_out), .in1(negator_1_out), .out(multiplexer_15_out), .sel(instruction_q[4]));
  Multiplexer #(.disabled("Z"), .enable("true"), .select(2), .width(16)) multiplexer_16 (
    .in0(adder_1_out), .in1(subtractor_1_out), .in2(multiplexer_14_out), .in3(multiplexer_11_out),
    .out(controlled_buffer_5_out), .sel(instruction_q[2:1]), .en(and_24_out));
  not not_4 (not_4_out, and_15_out);
  Multiplexer #(.disabled("Z"), .enable("true"), .select(2), .width(16)) multiplexer_17 (
    .in0(multiplexer_12_out), .in1(multiplexer_13_out), .out(controlled_buffer_5_out),
    .sel(instruction_q[2:1]), .en(and_15_out));  // open: in2, in3
  Multiplexer #(.select(4), .width(16)) multiplexer_18 (
    .in0({16{1'b0}}), .in1(FREQUENCY_in), .in2(d_ff_1_q), .out(SPECIAL_REG_OUT), .sel(SELECT_SPECIAL_REG));  // open: in3, in4, in5, in6, in7, in8, in9, in10, in11, in12, in13, in14, in15

  // Other names for the same wires on the sheet: READ_SPECIAL_B = READ_SPECIAL_A

  // Notes on the sheet:
  //   FLAGS
  //   MODEL
endmodule
